# Fritzing sketch 02_twopin_oneled_npn (saved by Fritzing 0.8.0b)
breadboards: 1

parts:
  part = Arduino Uno (Rev3)
  LED1 = LED - 5mm [color="Red (633nm)" package="5 mm [THT]"]
  R1 = Resistor [tolerance=±5% resistance=330 package=THT]
  NPN_2N3904 = NPN-Transistor [package="TO92 [THT]"]

nets:
  N1: part.GND, NPN_2N3904.E
  N2: part.D11_PWM/MOSI, NPN_2N3904.B
  N3: part.D2, R1.Pin_1
  N4: LED1.cathode, NPN_2N3904.C
  N5: LED1.anode, R1.Pin_0
