# Fritzing sketch 03_twopin_oneled_npnreversed (saved by Fritzing 0.8.0b)
breadboards: 1

parts:
  Part1 = Arduino Uno (Rev3)
  LED1 = LED - 5mm [color="Red (633nm)" package="5 mm [THT]"]
  R1 = Resistor [tolerance=±5% resistance=330 package=THT]
  Q1 = NPN-Transistor [package="TO92 [THT]"]

nets:
  N1: Part1.D11_PWM/MOSI, Q1.B
  N2: Part1.D2, LED1.cathode
  N3: Part1.3V3, Q1.C
  N4: LED1.anode, R1.Pin_0
  N5: R1.Pin_1, Q1.E
