# Fritzing sketch 04_rgbled (saved by Fritzing 0.8.0b)
breadboards: 1

parts:
  Part1 = Arduino Uno (Rev3)
  LED1 = RGB LED (com. anode, rbg) [package="5 mm [THT]"]
  R1 = Resistor [tolerance=±5% resistance=220 package=THT]
  Q1 = NPN-Transistor [package="TO92 [THT]"]
  Q2 = NPN-Transistor [package="TO92 [THT]"]
  Q3 = NPN-Transistor [package="TO92 [THT]"]

nets:
  N1: Part1.GND, Q1.E, Q2.E, Q3.E
  N2: Part1.D9_PWM, Q2.B
  N3: Part1.D10_PWM/SS, Q3.B
  N4: Part1.D11_PWM/MOSI, Q1.B
  N5: Part1.D2, R1.Pin_1
  N6: LED1.red_cathode, Q1.C
  N7: LED1.common_anode, R1.Pin_0
  N8: LED1.blue_cathode, Q2.C
  N9: LED1.green_cathode, Q3.C
