# Fritzing sketch 05_fecube_01 (saved by Fritzing 0.8.0b)
breadboards: 1

parts:
  LED1 = RGB LED (com. cathode, rbg) [package="5 mm [THT]"]
  LED2 = RGB LED (com. cathode, rbg) [package="5 mm [THT]"]
  LED3 = RGB LED (com. cathode, rbg) [package="5 mm [THT]"]
  LED4 = RGB LED (com. cathode, rbg) [package="5 mm [THT]"]
  LED5 = RGB LED (com. cathode, rbg) [package="5 mm [THT]"]
  LED6 = RGB LED (com. cathode, rbg) [package="5 mm [THT]"]
  LED7 = RGB LED (com. cathode, rbg) [package="5 mm [THT]"]
  LED8 = RGB LED (com. cathode, rbg) [package="5 mm [THT]"]
  LED9 = RGB LED (com. cathode, rbg) [package="5 mm [THT]"]
  R2 = Resistor [tolerance=±5% resistance=220 package=THT]
  R3 = Resistor [tolerance=±5% resistance=220 package=THT]
  R4 = Resistor [tolerance=±5% resistance=220 package=THT]
  R5 = Resistor [tolerance=±5% resistance=220 package=THT]
  R6 = Resistor [tolerance=±5% resistance=220 package=THT]
  R7 = Resistor [tolerance=±5% resistance=220 package=THT]
  R8 = Resistor [tolerance=±5% resistance=220 package=THT]
  R9 = Resistor [tolerance=±5% resistance=220 package=THT]
  R10 = Resistor [tolerance=±5% resistance=220 package=THT]

nets:
  N1: LED1.red_anode, LED2.red_anode, LED3.red_anode, LED4.red_anode, LED5.red_anode, LED6.red_anode, LED7.red_anode, LED8.red_anode, LED9.red_anode
  N2: LED1.common_cathode, R2.Pin_1
  N3: LED1.blue_anode, LED2.blue_anode, LED3.blue_anode, LED4.blue_anode, LED5.blue_anode, LED6.blue_anode, LED7.blue_anode, LED8.blue_anode, LED9.blue_anode
  N4: LED1.green_anode, LED2.green_anode, LED3.green_anode, LED4.green_anode, LED5.green_anode, LED6.green_anode, LED7.green_anode, LED8.green_anode, LED9.green_anode
  N5: LED2.common_cathode, R3.Pin_1
  N6: LED3.common_cathode, R4.Pin_1
  N7: LED4.common_cathode, R5.Pin_1
  N8: LED5.common_cathode, R6.Pin_1
  N9: LED6.common_cathode, R7.Pin_1
  N10: LED7.common_cathode, R8.Pin_1
  N11: LED8.common_cathode, R9.Pin_1
  N12: LED9.common_cathode, R10.Pin_1
