# Fritzing sketch 05_fecube_02 (saved by Fritzing 0.8.0b)
breadboards: 1

parts:
  Part1 = Arduino Uno (Rev3)
  LED1 = RGB LED (com. cathode, rbg) [package="5 mm [THT]"]
  LED2 = RGB LED (com. cathode, rbg) [package="5 mm [THT]"]
  LED3 = RGB LED (com. cathode, rbg) [package="5 mm [THT]"]
  LED4 = RGB LED (com. cathode, rbg) [package="5 mm [THT]"]
  LED5 = RGB LED (com. cathode, rbg) [package="5 mm [THT]"]
  LED6 = RGB LED (com. cathode, rbg) [package="5 mm [THT]"]
  LED7 = RGB LED (com. cathode, rbg) [package="5 mm [THT]"]
  LED8 = RGB LED (com. cathode, rbg) [package="5 mm [THT]"]
  LED9 = RGB LED (com. cathode, rbg) [package="5 mm [THT]"]
  Q1 = NPN-Transistor [package="TO92 [THT]"]
  Q2 = NPN-Transistor [package="TO92 [THT]"]
  Q3 = NPN-Transistor [package="TO92 [THT]"]
  R1 = Resistor [tolerance=±5% resistance=220 package=THT]
  R2 = Resistor [tolerance=±5% resistance=220 package=THT]
  R3 = Resistor [tolerance=±5% resistance=220 package=THT]
  R4 = Resistor [tolerance=±5% resistance=220 package=THT]
  R5 = Resistor [tolerance=±5% resistance=220 package=THT]
  R6 = Resistor [tolerance=±5% resistance=220 package=THT]
  R7 = Resistor [tolerance=±5% resistance=220 package=THT]
  R8 = Resistor [tolerance=±5% resistance=220 package=THT]
  R9 = Resistor [tolerance=±5% resistance=220 package=THT]

nets (from the breadboard view):
  N1: Part1.GND, Q1.E, Q2.E, Q3.E
  N2: Part1.D8, R2.Pin_0
  N3: Part1.D9_PWM, R1.Pin_0
  N4: Part1.D10_PWM/SS, Q3.B
  N5: Part1.D11_PWM/MOSI, Q2.B
  N6: Part1.D12/MISO, Q1.B
  N7: Part1.D1/TX, R9.Pin_0
  N8: Part1.D2, R8.Pin_0
  N9: Part1.D3_PWM, R7.Pin_0
  N10: Part1.D4, R6.Pin_0
  N11: Part1.D5_PWM, R5.Pin_0
  N12: Part1.D6_PWM, R4.Pin_0
  N13: Part1.D7, R3.Pin_0
  N14: LED1.red_anode, LED2.red_anode, LED3.red_anode, LED4.red_anode, LED5.red_anode, LED6.red_anode, LED7.red_anode, LED8.red_anode, LED9.red_anode, Q3.C
  N15: LED1.common_cathode, R1.Pin_1
  N16: LED1.blue_anode, LED2.blue_anode, LED3.blue_anode, LED4.blue_anode, LED5.blue_anode, LED6.blue_anode, LED7.blue_anode, LED8.blue_anode, LED9.blue_anode, Q2.C
  N17: LED1.green_anode, LED2.green_anode, LED3.green_anode, LED4.green_anode, LED5.green_anode, LED6.green_anode, LED7.green_anode, LED8.green_anode, LED9.green_anode, Q1.C
  N18: LED2.common_cathode, R2.Pin_1
  N19: LED3.common_cathode, R3.Pin_1
  N20: LED4.common_cathode, R4.Pin_1
  N21: LED5.common_cathode, R5.Pin_1
  N22: LED6.common_cathode, R6.Pin_1
  N23: LED7.common_cathode, R7.Pin_1
  N24: LED8.common_cathode, R8.Pin_1
  N25: LED9.common_cathode, R9.Pin_1
