# Fritzing sketch 05_pushbutton_01 (saved by Fritzing 0.8.0b)
breadboards: 1

parts:
  Part1 = Arduino Uno (Rev3)
  LED2 = LED - 5mm [color="Red (633nm)" package="5 mm [THT]"]
  R2 = Resistor [tolerance=±5% resistance=330 package=THT]
  pushbutton = Pushbutton [package="[THT]"]

nets:
  N1: Part1.GND, LED2.cathode
  N2: Part1.5V, pushbutton.Pin_1, pushbutton.Pin_2
  N3: LED2.anode, R2.Pin_0
  N4: R2.Pin_1, pushbutton.Pin_3, pushbutton.Pin_4
