# Fritzing sketch 05_pushbutton_02 (saved by Fritzing 0.8.0b)
breadboards: 1

parts:
  Part1 = Arduino Uno (Rev3)
  LED2 = LED - 5mm [color="Red (633nm)" package="5 mm [THT]"]
  R2 = Resistor [tolerance=±5% resistance=330 package=THT]
  S1 = Pushbutton [package="[THT]"]
  R3 = Resistor [tolerance=±5% resistance=10k package=THT]

nets:
  N1: Part1.5V, S1.Pin_3, S1.Pin_4
  N2: Part1.GND, LED2.cathode, R3.Pin_1
  N3: Part1.D13/SCK, R2.Pin_1
  N4: Part1.D2, S1.Pin_1, S1.Pin_2, R3.Pin_0
  N5: LED2.anode, R2.Pin_0
