# Fritzing sketch n01_rgbledtest (saved by Fritzing 0.8.5b)
breadboards: 1

parts:
  Part1 = Arduino Uno (Rev3)
  LED1 = RGB LED (com. cathode, rbg) [package="5 mm [THT]"]
  R1 = Resistor [tolerance=±5% resistance=220 package=THT]

nets:
  N1: Part1.GND, R1.Pin_0
  N2: Part1.5V, LED1.green_anode
  N3: LED1.common_cathode, R1.Pin_1
