# Fritzing sketch n02_rgbledsturing (saved by Fritzing 0.8.5b)
breadboards: 1

parts:
  Part1 = Arduino Uno (Rev3)
  LED1 = RGB LED (com. cathode, rbg) [package="5 mm [THT]"]
  R1 = Resistor [tolerance=±5% resistance=220 package=THT]

nets:
  N1: Part1.D8, LED1.red_anode
  N2: Part1.D9_PWM, LED1.blue_anode
  N3: Part1.D10_PWM/SS, LED1.green_anode
  N4: Part1.GND, R1.Pin_0
  N5: LED1.common_cathode, R1.Pin_1
