# Fritzing sketch n03_rgblednpn (saved by Fritzing 0.8.5b)
breadboards: 1

parts:
  Part1 = Arduino Uno (Rev3)
  LED1 = RGB LED (com. cathode, rbg) [package="5 mm [THT]"]
  R1 = Resistor [tolerance=±5% resistance=220 package=THT]
  Q1 = NPN-Transistor [package="TO92 [THT]"]
  Q2 = NPN-Transistor [package="TO92 [THT]"]
  Q3 = NPN-Transistor [package="TO92 [THT]"]
  R2 = Resistor [tolerance=±5% resistance=220 package=THT]
  R3 = Resistor [tolerance=±5% resistance=220 package=THT]
  R4 = Resistor [tolerance=±5% resistance=220 package=THT]

nets:
  N1: Part1.D8, R2.Pin_0
  N2: Part1.D9_PWM, R3.Pin_0
  N3: Part1.D10_PWM/SS, R4.Pin_0
  N4: Part1.GND, LED1.common_cathode
  N5: Part1.5V, R1.Pin_1
  N6: LED1.red_anode, Q1.C
  N7: LED1.blue_anode, Q2.C
  N8: LED1.green_anode, Q3.C
  N9: R1.Pin_0, Q1.E, Q2.E, Q3.E
  N10: Q1.B, R2.Pin_1
  N11: Q2.B, R3.Pin_1
  N12: Q3.B, R4.Pin_1
