# Fritzing sketch n04_rgbledmultiplex (saved by Fritzing 0.8.5b)
breadboards: 1

parts:
  Part1 = Arduino Uno (Rev3)
  LED1 = RGB LED (com. cathode, rbg) [package="5 mm [THT]"]
  R1 = Resistor [tolerance=±5% resistance=220 package=THT]
  Q1 = NPN-Transistor [package="TO92 [THT]"]
  Q2 = NPN-Transistor [package="TO92 [THT]"]
  Q3 = NPN-Transistor [package="TO92 [THT]"]
  R2 = Resistor [tolerance=±5% resistance=220 package=THT]
  R3 = Resistor [tolerance=±5% resistance=220 package=THT]
  R4 = Resistor [tolerance=±5% resistance=220 package=THT]
  LED2 = RGB LED (com. cathode, rbg) [package="5 mm [THT]"]

nets:
  N1: Part1.D8, R2.Pin_0
  N2: Part1.D9_PWM, R3.Pin_0
  N3: Part1.D10_PWM/SS, R4.Pin_0
  N4: Part1.D11_PWM/MOSI, LED2.common_cathode
  N5: Part1.D12/MISO, LED1.common_cathode
  N6: Part1.5V, R1.Pin_1
  N7: LED1.red_anode, Q1.C, LED2.red_anode
  N8: LED1.blue_anode, Q2.C, LED2.blue_anode
  N9: LED1.green_anode, Q3.C, LED2.green_anode
  N10: R1.Pin_0, Q1.E, Q2.E, Q3.E
  N11: Q1.B, R2.Pin_1
  N12: Q2.B, R3.Pin_1
  N13: Q3.B, R4.Pin_1
