# Fritzing sketch n06_pushbuttontest (saved by Fritzing 0.8.5b)
breadboards: 1

parts:
  R2 = Resistor [tolerance=±5% resistance=330 package=THT]
  Part1 = Arduino Uno (Rev3)
  LED3 = RGB LED (com. cathode, rbg) [package="5 mm [THT]"]
  pushbutton = Pushbutton [package="[THT]"]

nets:
  N1: R2.Pin_0, LED3.green_anode
  N2: R2.Pin_1, pushbutton.Pin_3, pushbutton.Pin_4
  N3: Part1.GND, LED3.common_cathode
  N4: Part1.5V, pushbutton.Pin_1, pushbutton.Pin_2
