# Fritzing sketch n07_pushbutton_status (saved by Fritzing 0.8.5b)
breadboards: 1

parts:
  Part1 = Arduino Uno (Rev3)
  S2 = Pushbutton [package="[THT]"]
  R4 = Resistor [tolerance=±5% resistance=10k package=THT]
  LED3 = RGB LED (com. anode, rbg) [package="5 mm [THT]"]
  R5 = Resistor [tolerance=±5% resistance=330 package=THT]

nets:
  N1: Part1.D12/MISO, S2.Pin_3, S2.Pin_4, R4.Pin_1
  N2: Part1.D13/SCK, R5.Pin_1
  N3: Part1.GND, R4.Pin_0, LED3.common_anode
  N4: Part1.5V, S2.Pin_1, S2.Pin_2
  N5: LED3.green_cathode, R5.Pin_0
