# Fritzing sketch n08_fecube_pushbtn (saved by Fritzing 0.8.5b)
breadboards: 1

parts:
  LED1 = RGB LED (com. cathode, rbg) [package="5 mm [THT]"]
  LED2 = RGB LED (com. cathode, rbg) [package="5 mm [THT]"]
  LED3 = RGB LED (com. cathode, rbg) [package="5 mm [THT]"]
  LED4 = RGB LED (com. cathode, rbg) [package="5 mm [THT]"]
  LED5 = RGB LED (com. cathode, rbg) [package="5 mm [THT]"]
  LED6 = RGB LED (com. cathode, rbg) [package="5 mm [THT]"]
  LED7 = RGB LED (com. cathode, rbg) [package="5 mm [THT]"]
  LED8 = RGB LED (com. cathode, rbg) [package="5 mm [THT]"]
  LED9 = RGB LED (com. cathode, rbg) [package="5 mm [THT]"]
  Q1 = NPN-Transistor [package="TO92 [THT]"]
  Q2 = NPN-Transistor [package="TO92 [THT]"]
  R1 = Resistor [tolerance=±5% resistance=220 package=THT]
  R2 = Resistor [tolerance=±5% resistance=220 package=THT]
  R3 = Resistor [tolerance=±5% resistance=220 package=THT]
  R4 = Resistor [tolerance=±5% resistance=220 package=THT]
  R5 = Resistor [tolerance=±5% resistance=220 package=THT]
  R6 = Resistor [tolerance=±5% resistance=220 package=THT]
  R7 = Resistor [tolerance=±5% resistance=220 package=THT]
  R8 = Resistor [tolerance=±5% resistance=220 package=THT]
  R9 = Resistor [tolerance=±5% resistance=220 package=THT]
  Q3 = NPN-Transistor [package="TO92 [THT]"]
  S2 = Pushbutton [package="[THT]"]
  R10 = Resistor [tolerance=±5% resistance=10k package=THT]
  Part1 = Arduino Uno (Rev3)

nets:
  N1: LED1.red_anode, LED2.red_anode, LED3.red_anode, LED4.red_anode, LED5.red_anode, LED6.red_anode, LED7.red_anode, LED8.red_anode, LED9.red_anode, Q3.E
  N2: LED1.common_cathode, R1.Pin_0, R1.Pin_1, Part1.D9_PWM
  N3: LED1.blue_anode, LED2.blue_anode, LED3.blue_anode, LED4.blue_anode, LED5.blue_anode, LED6.blue_anode, LED7.blue_anode, LED8.blue_anode, LED9.blue_anode, Q2.E
  N4: LED1.green_anode, LED2.green_anode, LED3.green_anode, LED4.green_anode, LED5.green_anode, LED6.green_anode, LED7.green_anode, LED8.green_anode, LED9.green_anode, Q1.E
  N5: LED2.common_cathode, R2.Pin_1
  N6: LED3.common_cathode, R3.Pin_1
  N7: LED4.common_cathode, R4.Pin_1
  N8: LED5.common_cathode, R5.Pin_1
  N9: LED6.common_cathode, R6.Pin_1
  N10: LED7.common_cathode, R7.Pin_1
  N11: LED8.common_cathode, R8.Pin_1
  N12: LED9.common_cathode, R9.Pin_1
  N13: Q1.B, Part1.D12/MISO
  N14: Q1.C, Q2.C, Q3.C, S2.Pin_3, S2.Pin_4, Part1.5V
  N15: Q2.B, Part1.D11_PWM/MOSI
  N16: R2.Pin_0, Part1.D8
  N17: R3.Pin_0, Part1.D7
  N18: R4.Pin_0, Part1.D6_PWM
  N19: R5.Pin_0, Part1.D5_PWM
  N20: R6.Pin_0, Part1.D4
  N21: R7.Pin_0, Part1.D3_PWM
  N22: R8.Pin_0, Part1.D2
  N23: R9.Pin_0, Part1.D1/TX
  N24: Q3.B, Part1.D10_PWM/SS
  N25: S2.Pin_1, S2.Pin_2, R10.Pin_0, Part1.D13/SCK
  N26: R10.Pin_1, Part1.GND
